# Fritzing sketch mqtt-gateway-with-temp (saved by Fritzing 0.9.3b)
breadboards: 1

parts:
  U3 = RF-LINK_RX [package=rf-link_rx]
  U4 = RF-LINK_TX [package=rf-link_tx]
  Bauteil1 = Adafruit BMP085 [part_number="Adafruit #391"]
  WeMos_D1_Mini1 = WeMos D1 Mini

nets:
  GND: U3.GND, U4.GND, Bauteil1.GND, WeMos_D1_Mini1.G
  N1: U3.DATA, WeMos_D1_Mini1.D5
  +5V: U3.+5V, U4.+5V, Bauteil1.VIN, WeMos_D1_Mini1.5V
  N2: U4.DATA, WeMos_D1_Mini1.D0
  N3: Bauteil1.SCL, WeMos_D1_Mini1.D1
  N4: Bauteil1.SDA, WeMos_D1_Mini1.D2

custom parts:
  Adafruit BMP085: This precision sensor from Bosch is the best low-cost sensing solution for measuring barometric pressure and temperature. Because pressure changes with altitude you can also use it as an altimeter! The sensor is soldered onto a PCB with a 3.3V regulator, I2C level shifter and pull-up resistors on the I2C pins. NEW! We now have a fully 5V compliant version of this board - a 3.3V regulator and a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
  WeMos D1 Mini: The D1 mini is a mini wifi board based on ESP-8266EX.
